# Fritzing sketch wiring (saved by Fritzing 0.9.3b)

parts:
  Part1 = Arduino Pro Mini (5V)
  7SEG1 = 7-Segment LED I2C Backpack (yellow)
  Part2 = PowerBoost 500 Charger
  BATT1 = LiPoly Battery (1300mAh)  # not connected

nets:
  N1: Part1.VCC, 7SEG1.V+, Part2.5.0V
  GND: Part1.GND, 7SEG1.GND, Part2.GND
  N2: Part1.A4, 7SEG1.SDA
  N3: Part1.A5, 7SEG1.SCL

notes:
  GND
  CTS
  5V
  TXD
  RXD
  DTR
  green-RX of RFID
  yellow-TX of RFID
  black-V- of RFID
  red-V+ of RFID
  to CP2102 USB to TTL

custom parts:
  7-Segment LED I2C Backpack (yellow): 4-digit, 7-segment LED Display with I2C Control
  PowerBoost 500 Charger: The PowerBoost 500C is a little DC/DC boost converter module that can be powered by any 3.7V LiIon/LiPoly battery, and convert the battery output to 5.2V DC for running your 5V projects. At its heart is a TPS61090 boost converter from TI. This boost converter chip has some really nice extras such as low battery detection, 2A internal switch, synchronous conversion, excellent efficiency, and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
  LiPoly Battery (1300mAh): Lithium Ion Polymer Battery (1300mAh)
